# Fritzing sketch circuit(1) (saved by Fritzing 0.9.6b)
breadboards: 1

parts:
  J1 = STM32 Nucleo boards
  Componente1 = Arduino Uno (Rev3) - ICSP
  HC-SR04_Sensor_1 = HC-SR04 Ultrasonic Distance Sensor
  J2 = Piezo Speaker
  Componente2 = InvenSense MPU6050
  BN-880 = SUP500F [package=sup500f]  # not connected
  R1 = Resistor [tolerance=±5% power=0.25 resistance=220 package=THT]
  IC2 = ULN2003A [package="SO16 [SMD]"]
  M1 = Stepper Motor - Unipolar
  Componente3 = Bluetooth HC-05 Macho

nets:
  GND: J1.GND, Componente1.GND
  N1: Componente1.D8, IC2.In_4
  N2: Componente1.D9_PWM, IC2.In_3
  N3: Componente1.D10_PWM/SS, IC2.In_2
  N4: Componente1.D11_PWM/MOSI, IC2.In_1
  N5: Componente1.D12/MISO, HC-SR04_Sensor_1.TRIG
  N6: Componente1.D13/SCK, HC-SR04_Sensor_1.ECHO
  N7: Componente1.D2, Componente3.RXD
  N8: Componente1.D3_PWM, Componente3.TXD
  N9: HC-SR04_Sensor_1.VCC, M1.COMMON_1, M1.COMMON_2
  GND_2: HC-SR04_Sensor_1.GND, Componente2.GND, R1.Pin_1
  N10: J2.pin1, R1.Pin_0
  N11: IC2.Out_3, M1.B
  N12: IC2.Out_1, M1.A

notes:
  BN-880:
  GND: Black
  VCC: Red
  TX: Green
